# Fritzing sketch ringer4 (saved by Fritzing 0.9.3b)
circuit board: 8.53488cm x 5.63626cm
breadboards: 1

parts:
  Q1 = Basic FET P-Channel [package="TO220 [THT]"]
  Bell = Screw terminal - 2 pins [package=THT]
  Magneto = Screw terminal - 2 pins [package=THT]
  Hook_SW = Screw terminal - 2 pins [package=THT]
  Raspberry_Pi_1 = Raspberry Pi 3 [part_number=RPI-3-V1.2]
  ACT = LED - 3mm [color="Red (633nm)" package="3 mm [THT]"]
  IC2 = NJM2670 [package="NJM2670D2 (DIP22)"]
  R2 = Resistor [tolerance=±5% resistance=180 package=THT]
  D1 = Schottky Diode [part_number=1N5817 package="300 mil [THT]"]
  R1 = Resistor [tolerance=±5% resistance=1k package=THT]
  C1 = Ceramic Capacitor [capacitance=1nF package="100 mil [THT, multilayer]"]
  C4 = Electrolytic Capacitor [capacitance=100µF voltage=50V package="200 mil [THT, electrolytic]"]
  R4 = Resistor [tolerance=±5% resistance=47k package=THT]
  R5 = Resistor [tolerance=±5% resistance=1k package=THT]
  IC1 = MC34063AP [chip_label=IC package="DIP (Dual Inline) [THT]"]
  C2 = Electrolytic Capacitor [capacitance=100µF package="100 mil [THT, electrolytic]"]
  C3 = Ceramic Capacitor [capacitance=100nF package="100 mil [THT, multilayer]"]
  C5 = Electrolytic Capacitor [capacitance=3.3µF voltage=50V package="100 mil [THT, electrolytic]"]
  L1 = RCP1317 [package="13 cm [THT]"]
  R3 = 0.22 Ω Resistor [package=THT]
  U1 = RT314F03 [part_number=RT314F03 package=OJ]
  Q2 = NPN-Transistor [package="TO92 [THT]"]
  Q3 = NPN-Transistor [package="TO92 [THT]"]
  R6 = Resistor [tolerance=±5% resistance=1k package=THT]
  R7 = Resistor [tolerance=±5% resistance=1k package=THT]
  IC3 = PDIP06 [chip_label=IC part_number=H11AA1SM package=PDIP]
  R8 = Resistor [tolerance=±5% resistance=470k package="0603 [SMD]"]
  R9 = Resistor [tolerance=±5% resistance=470k package="0603 [SMD]"]
  D5 = Rectifier Diode [package="Melf DO-213 AA [SMD]"]
  D6 = Rectifier Diode [package="Melf DO-213 AA [SMD]"]

nets:
  N1: Q1.gate, Raspberry_Pi_1.GPIO4
  VCC: Q1.drain, IC2.ENABLE_A, IC2.VCC, R5.Pin_0, IC1.VCC, C2.+, C3.0, R3.Pin_0
  N2: Q1.source, Raspberry_Pi_1.5V
  N3: Bell.pin1, Magneto.pin1, IC2.OUT_A1, R8.Pin_1
  N4: Bell.pin2, C5.-, U1.12#5, U1.11, U1.14
  N5: Magneto.pin2, U1.12#4, R9.Pin_1
  GND: Hook_SW.pin1, Raspberry_Pi_1.GND, ACT.cathode, IC2.SENSE_A, IC2.GND, IC2.ENABLE_B, R1.Pin_1, C1.0, C4.-, IC1.Switch_Emitter, IC1.GND, C2.-, C3.1, Q2.E, Q3.E, IC3.4
  N6: Hook_SW.pin2, Raspberry_Pi_1.GPIO19
  3V3: Raspberry_Pi_1.3v3, Raspberry_Pi_1.3V3, U1.A3, D5.cathode, D6.cathode
  N7: Raspberry_Pi_1.GPIO27, IC2.IN_A
  N8: Raspberry_Pi_1.GPIO22, IC2.IN_A2
  N9: Raspberry_Pi_1.GPIO5, R6.Pin_0
  N10: Raspberry_Pi_1.GPIO6, R7.Pin_0
  N11: Raspberry_Pi_1.GPIO26, IC3.5
  N12: ACT.anode, R5.Pin_1
  N13: IC2.OUT_A2, C5.+
  N14: IC2.VS_A, D1.anode, C4.+, R4.Pin_1
  N15: R2.Pin_0, IC1.Drive_Collector
  N16: R2.Pin_1, IC1.Ipk, L1.pin_0, R3.Pin_1
  N17: D1.cathode, IC1.Switch_Collector, L1.pin_1
  N18: R1.Pin_0, R4.Pin_0, IC1.Comparator_Inverting_Input
  N19: C1.1, IC1.Timing_Capacitor
  N20: U1.A1, Q3.C, D6.anode
  N21: U1.A2, Q2.C, D5.anode
  N22: Q2.B, R6.Pin_1
  N23: Q3.B, R7.Pin_1
  N24: IC3.1, R8.Pin_0
  N25: IC3.2, R9.Pin_0

notes:
  * Adjust boost/buck resistors to dial in ~30v
  * Adjust pad footprint of 4N35S
  cranky rev. A
  Magneto
  Driver
  +3.3v
  (output)

custom parts:
  RCP1317: Inductor
  0.22 Ω Resistor: BPR58 0.22 Ω 5W Resistor
  RT314F03: Two-coil bistable SPDT Relay
